# Fritzing sketch schema led chenillar (saved by Fritzing 0.9.10b)
breadboards: 1

parts:
  Composant1 = Arduino Uno (Rev3)
  LED1 = LED - 5mm [color="Red (633nm)" current=0.030 package="5 mm [THT]"]
  LED2 = LED - 5mm [color="Red (633nm)" current=0.030 package="5 mm [THT]"]
  LED3 = LED - 5mm [color="Red (633nm)" current=0.030 package="5 mm [THT]"]
  LED4 = LED - 5mm [color="Red (633nm)" current=0.030 package="5 mm [THT]"]
  LED5 = LED - 5mm [color="Red (633nm)" current=0.030 package="5 mm [THT]"]
  LED6 = LED - 5mm [color="Red (633nm)" current=0.030 package="5 mm [THT]"]
  LED7 = LED - 5mm [color="Red (633nm)" current=0.030 package="5 mm [THT]"]
  LED8 = LED - 5mm [color="Red (633nm)" current=0.030 package="5 mm [THT]"]
  LED9 = LED - 5mm [color="Red (633nm)" current=0.030 package="5 mm [THT]"]
  S1 = Pushbutton [package="[THT]"]
  R1 = Rotary Potentiometer (Small) [maximum_resistance=100kΩ knob_status=50% power=0.5W package=THT]

nets:
  N1: Composant1.A5/SCL, R1.wiper
  N2: Composant1.D8, LED1.anode
  N3: Composant1.D9_PWM, LED7.anode
  N4: Composant1.D10_PWM/SS, LED8.anode
  N5: Composant1.D13/SCK, S1.Pin_1, S1.Pin_2
  N6: Composant1.D2, LED9.anode
  N7: Composant1.D3_PWM, LED6.anode
  N8: Composant1.D4, LED5.anode
  N9: Composant1.D5_PWM, LED4.anode
  N10: Composant1.D6_PWM, LED2.anode
  N11: Composant1.D7, LED3.anode
  N12: Composant1.5V, LED3.cathode, R1.leg1
  N13: Composant1.GND, LED1.cathode, LED2.cathode, LED4.cathode, LED5.cathode, LED6.cathode, LED7.cathode, LED8.cathode, LED9.cathode, S1.Pin_3, S1.Pin_4, R1.leg2
